# Fritzing sketch Prototype Circuit (saved by Fritzing 0.7.12b)
breadboards: 1

parts:
  LCD1 = LCD screen
  U1 = Arduino Mega
  Part1 = Arduino Cellular Shield
  LED2 = LED - 5mm [color="Yellow (595nm)" package="5 mm [THT]"]
  R1 = Resistor [tolerance=±5% resistance=330 package=THT]
  R2 = Resistor [tolerance=±5% resistance=330 package=THT]
  LED3 = LED - 5mm [color="Red (635nm)" package="5 mm [THT]"]
  R4 = Resistor [tolerance=±5% resistance=330 package=THT]
  R3 = Resistor [tolerance=±5% resistance=1.5k package=THT]
  Power_plug1 = Power plug

nets:
  GND: LCD1.VSS, LCD1.R/W, LCD1.LED-, U1.GND, Part1.GND, R1.Pin_0, R2.Pin_0, Power_plug1.GND
  VDD: LCD1.VDD, U1.+5V, Part1.5V
  N1: LCD1.V0, R4.Pin_1, R3.Pin_0
  N2: LCD1.RS, U1.D12, Part1.D12
  N3: LCD1.E, U1.D11, Part1.D11
  N4: LCD1.DB4, U1.D10, Part1.D10
  N5: LCD1.DB5, U1.D9, Part1.D9
  N6: LCD1.DB6, U1.D8, Part1.D8
  N7: LCD1.DB7, U1.D7, Part1.D7
  VIN: LCD1.LED+, U1.VIN, Part1.VRAW, LED3.cathode, R4.Pin_0, Power_plug1.VCC
  N8: U1.D13, Part1.D13, LED2.cathode, R3.Pin_1
  N9: U1.RST, Part1.RESET
  N10: U1.D18, Part1.D-TX
  N11: U1.D19, Part1.D-RX
  N12: LED2.anode, R1.Pin_1
  N13: R2.Pin_1, LED3.anode

notes:
  6V/1.5-2A
